# Fritzing sketch HomeyLedDimmer_v1-0 (saved by Fritzing 0.9.3b)
circuit board: 5.6cm x 3.6cm

parts:
  IRLZ44N = STP16NF06 N-Channel Power MOSFET
  J1 = screw terminal, 2 pins
  J2 = screw terminal, 2 pins
  J3 = screw terminal, 2 pins
  C2 = Capacitor Polarized [package=cpol-radial-10uf-25v]
  100nF = Capacitor [package=cap-pth-5mm]
  LD1117v33 = Voltage Regulator -- 3.3 V -- LM1117
  R2 = Resistor [tolerance=±5% resistance=1k package=THT]
  R1 = Resistor [tolerance=±5% resistance=220k package=THT]
  WeMos_D1_Mini2 = WeMos D1 Mini

nets:
  N1: IRLZ44N.gate, R2.Pin_0, R1.Pin_0
  N2: IRLZ44N.drain, J2.pin2
  N3: IRLZ44N.source, J1.pin1, J3.pin1, C2.-, 100nF.2, LD1117v33.GND, R1.Pin_1, WeMos_D1_Mini2.G
  N4: J1.pin2, WeMos_D1_Mini2.D3
  N5: J2.pin1, J3.pin2, 100nF.1, LD1117v33.IN
  N6: C2.+, LD1117v33.OUT, WeMos_D1_Mini2.3V3
  N7: R2.Pin_1, WeMos_D1_Mini2.D5

notes:
  12 vdc
  +
  -
  Voltage Regulator LD1117v33 - 3.3 VDC
  MOSFET
  Push button
  LED
  Capacitor 10uF
  Capacitor 100nF
  +12V-
  -LED+
  Button
  HomeyLedDimmer v1.0
  1k
  10 uF
  100nF
  220k

custom parts:
  STP16NF06 N-Channel Power MOSFET: STP16NF06 N-channel Power MOSFET
  Voltage Regulator -- 3.3 V -- LM1117: LM1117-3.3 Voltage regulator, 3.3 V output. Note that the pinout order is not the same as LM7805 or LM7833.
